# Fritzing sketch Untitled Sketch (saved by Fritzing 0.9.3b)
breadboards: 1

parts:
  元件1 = Arduino Uno (Rev3)
  LED2 = LED - 5mm [color="Red (633nm)" package="5 mm [THT]"]
  R2 = Resistor [tolerance=±5% resistance=220 package=THT]
  R3 = Resistor [tolerance=±5% resistance=220 package=THT]
  LED3 = LED - 5mm [color="Red (633nm)" package="5 mm [THT]"]

nets:
  N1: 元件1.D10_PWM/SS, R2.Pin_1
  N2: 元件1.D13/SCK, R3.Pin_1
  N3: 元件1.GND, LED2.cathode, LED3.cathode
  N4: LED2.anode, R2.Pin_0
  N5: R3.Pin_0, LED3.anode
